# Fritzing sketch convertTrigger (saved by Fritzing 1.0.2b)

parts:
  Part1 = Arduino Uno (Rev3)
  Trigger_in = BNC [package=bnc]
  Trigger_out = BNC [package=bnc]

nets:
  GND: Part1.GND, Trigger_in.GND, Trigger_out.GND
  N1: Part1.D2, Trigger_in.OUT
  N2: Part1.D4, Trigger_out.OUT

notes:
  Trigger in: a short triggering (e.g., a 1 us pulse) signal. For UNO, pin 2 or 3 can be configured as an interrupt pin.
  Trigger out: A long triggering signal (e.g., a 2ms pulse)
