# Fritzing sketch flashing leds (saved by Fritzing 1.0.2b)

parts:
  Part1 = Arduino Uno (Rev3)
  Trigger_in = BNC [package=bnc]
  LED2 = LED - 5mm [color="White (4500K)" current=0.030A package="5 mm [THT]"]
  R1 = Resistor [tolerance=±5% power=0.25W resistance=1k package=THT]

nets:
  GND: Part1.GND, Trigger_in.GND, LED2.cathode
  N1: Part1.D2, Trigger_in.OUT
  N2: Part1.D4, R1.Pin_1
